// Digital circuit simulation.dig as structural Verilog
module simulation (
  input  in_1,
  input  in_2,
  input  in_3,
  input  in_4,
  input  in_5,
  input  in_6,
  input  in_7,
  input  in_8,
  input  in_9,
  input  in_10,
  input  in_11,
  input  in_12,
  output out_13,
  output out_14
);

  main_project #(.applicationType("GHDL")) u_main_project (
    .s0(in_7), .s1(in_1), .s2(in_8), .e1(in_2), .i0(in_9), .i1(in_3), .i2(in_4), .i3(in_5), .i4(in_6),
    .i5(in_10), .i6(in_11), .i7(in_12), .z(out_13), .z_invertido(out_14));
endmodule

/* Code of main_project:
library IEEE;
use IEEE.std_logic_1164.all;

entity main_project is
port(
	s0,s1,s2,e1 : in std_logic;
	i0,i1,i2,i3,i4,i5,i6,i7 : in std_logic;
	z , z_invertido : out std_logic
	);
end main_project;

architecture implementar of main_project is
begin
	process(s0,s1,s2,e1,i0,i1,i2,i3,i4,i5,i6,i7)
	begin
	if e1 = '1' then
		if (s2='0' and s1='0' and s0='0') then
			z <= i0;
			z_invertido <= not i0;
		elsif (s2='0' and s1='0' and s0='1') then
			z <= i1;
			z_invertido <= not i1;
		elsif (s2='0' and s1='1' and s0='0') then
			z <= i2;
			z_invertido <= not i2;
		elsif (s2='0' and s1='1' and s0='1') then
			z <= i3;
			z_invertido <= not i3;
		elsif (s2='1' and s1='0' and s0='0') then
			z <= i4;
			z_invertido <= not i4;
		elsif (s2='1' and s1='0' and s0='1') then
			z <= i5;
			z_invertido <= not i5;
		elsif (s2='1' and s1='1' and s0='0') then
			z <= i6;
			z_invertido <= not i6;
		elsif (s2='1' and s1='1' and s0='1') then
			z <= i7;
			z_invertido <= not i7;
		end if;
	else
		z <= '0';
		z_invertido <= '1';
	end if;
	end process;
end implementar;
*/
